# Fritzing sketch OSWaLD_schematics (saved by Fritzing 1.0.2b)
breadboards: 1

parts:
  Mod1 = Raspberry Pi Pico W
  Squix1 = OLED 0.96" 128x64 I2C SSD1306
  LED1 = LED - 5mm [color="Green (560nm)" current=0.030A package="5 mm [THT]"]  # not connected
  LED2 = LED - 5mm [color="Red (633nm)" current=0.030A package="5 mm [THT]"]  # not connected
  R1 = Resistor [tolerance=±5% power=0.25W resistance=220 package=THT]  # not connected
  R2 = Resistor [tolerance=±5% power=0.25W resistance=220 package=THT]  # not connected
  S1 = Pushbutton [package="[THT]"]

nets:
  N1: Mod1.pin_3, Mod1.pin_8, Mod1.pin_13, Mod1.pin_18, Mod1.pin_23, Mod1.pin_28, Mod1.pin_33, Mod1.pin_38, Mod1.pin_42, Squix1.GND
  N2: Mod1.pin_4, Squix1.SCL
  N3: Mod1.pin_5, Squix1.SCA
  N4: Mod1.pin_6, S1.Pin_1, S1.Pin_2
  N5: Mod1.pin_37, Squix1.VCC, S1.Pin_3, S1.Pin_4

custom parts:
  Raspberry Pi Pico W: Raspberry Pi Pico W. Based around the RP2040 microcontroller the Pico W is a low cost microcontroller device bringing Raspberry Pi quality, cost, and easy of use to the microcontroller space. The areas marked KEEPOUT in pcb silkscreen should not have traces running through them to avoid shorts on a soldered in module!
